# Fritzing sketch gpio_midi (saved by Fritzing 0.9.3b)
breadboards: 1

parts:
  U1 = MIDI_CONN_FEMALE [package=din_5_female]
  R1 = Resistor [tolerance=±5% resistance=220 package="0402 [SMD]"]
  D2 = Rectifier Diode [part_number=1N4001 package="300 mil [THT]"]
  IC1 = IC, DIP package, 8 pins [chip_label=6N138]
  R2 = Resistor [tolerance=±5% resistance=10k package="0402 [SMD]"]
  R3 = Resistor [tolerance=±5% resistance=1k package="0402 [SMD]"]
  Raspberry_Pi_1 = Raspberry Pi 3 [part_number=RPI-3-V1.2]

nets:
  N1: U1.MIDI_IN, R1.Pin_1
  N2: U1.MIDI_OUT, D2.anode, IC1.pin3
  N3: R1.Pin_0, D2.cathode, IC1.pin2
  N4: IC1.pin5, R2.Pin_1, Raspberry_Pi_1.GND
  N5: IC1.pin6, R3.Pin_0, Raspberry_Pi_1.GPIO15
  N6: IC1.pin7, R2.Pin_0
  N7: IC1.pin8, R3.Pin_1, Raspberry_Pi_1.3v3
